# Fritzing sketch sketch (saved by Fritzing 0.9.3b)
breadboards: 1

parts:
  OLED = adafruit [part_number="Adafruit #3527"]
  DHT11 = DHT11_Temperature_and_Humitidy_Sensor
  WeMos_D1_Mini1 = WeMos D1 Mini
  Switch = SWITCH-MOMENTARY-2 [package=tactile-pth]

nets:
  N1: OLED.connector2, WeMos_D1_Mini1.D2
  N2: OLED.connector3, DHT11.connector1, WeMos_D1_Mini1.5V
  N3: OLED.connector4, WeMos_D1_Mini1.D1
  N4: OLED.connector5, DHT11.connector4, WeMos_D1_Mini1.G, Switch.2
  N5: DHT11.connector2, WeMos_D1_Mini1.D5
  N6: WeMos_D1_Mini1.D3, Switch.1
